// Logisim project ELEVADOR LOGSIM.circ as structural Verilog: 5 circuits, main circuit elevador (main)
// decod 7 seg
module display_7 (
  input  andar_0,
  input  andar_1,
  input  andar_2,
  output a,
  output b,
  output c,
  output d,
  output e,
  output f,
  output g,
  output ponto
);

  wire and_1_out, and_2_out, and_3_out, and_4_out, and_5_out, and_6_out, and_7_out, and_8_out, and_9_out,
       and_10_out, and_11_out, not_1_out, not_2_out, not_3_out, not_4_out, not_5_out, not_6_out, not_7_out,
       not_8_out, not_9_out, not_10_out, not_11_out, not_12_out, not_13_out, not_14_out, not_15_out,
       not_16_out, not_17_out, not_18_out, not_19_out, not_20_out, not_21_out, not_22_out, not_23_out,
       not_24_out, not_25_out, not_26_out;

  not not_1 (not_1_out, andar_0);
  not not_2 (not_2_out, andar_1);
  not not_3 (not_3_out, andar_1);
  not not_4 (not_4_out, andar_2);
  not not_5 (not_5_out, andar_0);
  not not_6 (not_6_out, andar_1);
  not not_7 (not_7_out, andar_0);
  not not_8 (not_8_out, andar_2);
  not not_9 (not_9_out, andar_1);
  not not_10 (not_10_out, andar_2);
  not not_11 (not_11_out, andar_0);
  not not_12 (not_12_out, andar_2);
  not not_13 (not_13_out, andar_1);
  not not_14 (not_14_out, andar_2);
  not not_15 (not_15_out, andar_0);
  not not_16 (not_16_out, andar_1);
  not not_17 (not_17_out, andar_1);
  not not_18 (not_18_out, andar_2);
  not not_19 (not_19_out, andar_0);
  not not_20 (not_20_out, andar_1);
  not not_21 (not_21_out, andar_1);
  not not_22 (not_22_out, andar_2);
  not not_23 (not_23_out, andar_1);
  not not_24 (not_24_out, andar_2);
  not not_25 (not_25_out, andar_0);
  not not_26 (not_26_out, andar_1);
  and and_1 (and_1_out, not_1_out, not_2_out, andar_2);
  and and_2 (and_2_out, andar_0, not_3_out, not_4_out);
  and and_3 (and_3_out, not_5_out, not_6_out, andar_2);
  and and_4 (and_4_out, not_7_out, andar_1, not_8_out);
  and and_5 (and_5_out, andar_0, not_9_out, not_10_out);
  and and_6 (and_6_out, not_11_out, andar_1, not_12_out);
  and and_7 (and_7_out, andar_0, not_13_out, not_14_out);
  and and_8 (and_8_out, not_15_out, not_16_out, andar_2);
  and and_9 (and_9_out, andar_0, not_17_out, not_18_out);
  and and_10 (and_10_out, not_19_out, not_20_out, andar_2);
  and and_11 (and_11_out, andar_0, not_21_out, not_22_out);
  and and_12 (f, andar_0, not_23_out, not_24_out);
  and and_13 (g, not_25_out, not_26_out, andar_2);
  or or_1 (a, and_1_out, and_2_out);
  or or_2 (b, and_3_out, and_4_out, and_5_out);
  or or_3 (c, and_6_out, and_7_out);
  or or_4 (d, and_8_out, and_9_out);
  or or_5 (e, and_10_out, and_11_out);

  assign ponto = 1'b1;
endmodule

// logica dos leds
module logica (
  input  esta_no_terreo,
  input  ch_1_andar_do_terreo,
  input  ch_2_andar_do_terro,
  input  ch_chamada_chao,
  input  chamada1andar,
  input  chamada2andar,
  input  _0_elevaor,
  input  _1_elevador,
  input  _2_elevadr,
  output andar_0,
  output andar_1,
  output andar_2,
  output parado_pronto,
  output porta,
  output pra_cima,
  output pra_baixo
);

  wire and_1_out, and_2_out, and_3_out, and_4_out, and_5_out, and_6_out, and_7_out, and_8_out, and_9_out,
       and_10_out, and_11_out, and_12_out, and_13_out, and_14_out, and_15_out, and_16_out, and_17_out,
       and_18_out, and_19_out, and_20_out, and_21_out, and_22_out, and_23_out, and_24_out, and_25_out,
       and_26_out, and_27_out, and_28_out, and_29_out, and_30_out, and_31_out, and_32_out, and_33_out,
       and_34_out, and_35_out, and_36_out, and_37_out, and_38_out, and_39_out, and_40_out, and_41_out,
       and_42_out, and_43_out, not_1_out, not_2_out, not_3_out, not_4_out, not_5_out, not_6_out, not_7_out,
       not_8_out, not_9_out, not_10_out, not_11_out, not_12_out, not_13_out, not_14_out, not_15_out,
       not_16_out, not_17_out, not_18_out, not_19_out, not_20_out, not_21_out, not_22_out, not_23_out,
       not_24_out, not_25_out, not_26_out, not_27_out, not_28_out, not_29_out, not_30_out, not_31_out,
       not_32_out, not_33_out, not_34_out, not_35_out, not_36_out, not_37_out, not_38_out, not_39_out,
       not_40_out, not_41_out, not_42_out;

  not not_1 (not_1_out, ch_1_andar_do_terreo);
  not not_2 (not_2_out, ch_2_andar_do_terro);
  not not_3 (not_3_out, chamada1andar);
  not not_4 (not_4_out, chamada2andar);
  not not_5 (not_5_out, _1_elevador);
  not not_6 (not_6_out, _2_elevadr);
  not not_7 (not_7_out, ch_chamada_chao);
  not not_8 (not_8_out, chamada2andar);
  not not_9 (not_9_out, _0_elevaor);
  not not_10 (not_10_out, _2_elevadr);
  not not_11 (not_11_out, ch_chamada_chao);
  not not_12 (not_12_out, chamada1andar);
  not not_13 (not_13_out, _0_elevaor);
  not not_14 (not_14_out, _1_elevador);
  not not_15 (not_15_out, ch_2_andar_do_terro);
  not not_16 (not_16_out, ch_1_andar_do_terreo);
  not not_17 (not_17_out, esta_no_terreo);
  not not_18 (not_18_out, ch_2_andar_do_terro);
  not not_19 (not_19_out, ch_1_andar_do_terreo);
  not not_20 (not_20_out, ch_2_andar_do_terro);
  not not_21 (not_21_out, ch_1_andar_do_terreo);
  not not_22 (not_22_out, ch_1_andar_do_terreo);
  not not_23 (not_23_out, esta_no_terreo);
  not not_24 (not_24_out, ch_2_andar_do_terro);
  not not_25 (not_25_out, ch_chamada_chao);
  not not_26 (not_26_out, chamada1andar);
  not not_27 (not_27_out, _0_elevaor);
  not not_28 (not_28_out, _1_elevador);
  not not_29 (not_29_out, esta_no_terreo);
  not not_30 (not_30_out, chamada2andar);
  not not_31 (not_31_out, _2_elevadr);
  not not_32 (not_32_out, ch_2_andar_do_terro);
  not not_33 (not_33_out, ch_2_andar_do_terro);
  and and_1 (and_1_out, ch_2_andar_do_terro, _0_elevaor);
  and and_2 (and_2_out, ch_2_andar_do_terro, ch_chamada_chao);
  and and_3 (and_3_out, ch_1_andar_do_terreo, not_7_out, not_8_out, not_9_out, not_10_out);
  and and_4 (and_4_out, esta_no_terreo, _2_elevadr);
  and and_5 (and_5_out, esta_no_terreo, chamada2andar);
  not not_34 (not_34_out, esta_no_terreo);
  and and_6 (and_6_out, not_34_out, _2_elevadr);
  not not_35 (not_35_out, esta_no_terreo);
  and and_7 (and_7_out, not_35_out, chamada2andar);
  and and_8 (and_8_out, ch_2_andar_do_terro, not_11_out, not_12_out, not_13_out, not_14_out);
  and and_9 (and_9_out, not_15_out, _2_elevadr);
  and and_10 (and_10_out, not_16_out, _1_elevador);
  and and_11 (and_11_out, not_17_out, _0_elevaor);
  and and_12 (and_12_out, not_18_out, chamada2andar);
  and and_13 (and_13_out, not_19_out, chamada1andar);
  and and_14 (and_14_out, ch_2_andar_do_terro, ch_chamada_chao);
  and and_15 (and_15_out, ch_1_andar_do_terreo, ch_chamada_chao);
  and and_16 (and_16_out, not_20_out, _2_elevadr);
  and and_17 (and_17_out, not_21_out, _1_elevador);
  and and_18 (and_18_out, not_22_out, chamada1andar);
  and and_19 (and_19_out, ch_2_andar_do_terro, _0_elevaor);
  and and_20 (and_20_out, ch_2_andar_do_terro, ch_chamada_chao);
  and and_21 (and_21_out, ch_1_andar_do_terreo, _0_elevaor);
  and and_22 (and_22_out, ch_1_andar_do_terreo, chamada2andar);
  and and_23 (and_23_out, ch_1_andar_do_terreo, ch_chamada_chao);
  and and_24 (and_24_out, esta_no_terreo, chamada2andar);
  not not_36 (not_36_out, ch_2_andar_do_terro);
  not not_37 (not_37_out, ch_1_andar_do_terreo);
  not not_38 (not_38_out, ch_2_andar_do_terro);
  not not_39 (not_39_out, ch_1_andar_do_terreo);
  not not_40 (not_40_out, ch_2_andar_do_terro);
  not not_41 (not_41_out, ch_1_andar_do_terreo);
  not not_42 (not_42_out, ch_2_andar_do_terro);
  and and_25 (and_25_out, ch_2_andar_do_terro, _1_elevador);
  and and_26 (and_26_out, not_29_out, ch_2_andar_do_terro, not_30_out, _0_elevaor, not_31_out);
  and and_27 (and_27_out, ch_2_andar_do_terro, chamada1andar);
  and and_28 (and_28_out, ch_2_andar_do_terro, ch_chamada_chao);
  and and_29 (and_29_out, ch_1_andar_do_terreo, _0_elevaor);
  and and_30 (and_30_out, ch_1_andar_do_terreo, chamada2andar, _2_elevadr);
  and and_31 (and_31_out, ch_1_andar_do_terreo, chamada2andar, _1_elevador);
  and and_32 (and_32_out, ch_1_andar_do_terreo, chamada1andar, chamada2andar);
  and and_33 (and_33_out, ch_1_andar_do_terreo, ch_chamada_chao);
  and and_34 (and_34_out, ch_1_andar_do_terreo, ch_2_andar_do_terro, chamada2andar);
  and and_35 (and_35_out, esta_no_terreo, ch_1_andar_do_terreo, chamada2andar);
  and and_36 (and_36_out, not_1_out, not_2_out, not_3_out, not_4_out, not_5_out, not_6_out);
  or or_1 (andar_0, and_36_out, and_37_out, and_38_out);
  and and_37 (and_37_out, not_32_out, _0_elevaor);
  and and_38 (and_38_out, not_33_out, ch_chamada_chao);
  or or_2 (andar_2, and_6_out, and_7_out, and_8_out);
  or or_3 (parado_pronto, and_9_out, and_10_out, and_11_out, and_12_out, and_13_out, and_14_out, and_15_out);
  and and_39 (and_39_out, not_36_out, _2_elevadr);
  and and_40 (and_40_out, not_37_out, not_38_out, _1_elevador);
  and and_41 (and_41_out, not_23_out, not_24_out, not_25_out, not_26_out, chamada2andar, not_27_out, not_28_out);
  and and_42 (and_42_out, not_39_out, not_40_out, chamada2andar);
  and and_43 (and_43_out, not_41_out, not_42_out, chamada1andar);
  or or_4 (andar_1, _1_elevador, chamada1andar, and_1_out, and_2_out, and_3_out, and_4_out, and_5_out);
  or or_5 (porta, and_16_out, and_17_out, and_18_out, and_19_out, and_20_out, and_21_out, and_22_out, and_23_out, and_24_out);
  or or_6 (pra_cima, and_39_out, and_40_out, and_41_out, and_42_out, and_43_out);
  or or_7 (pra_baixo, and_25_out, and_26_out, and_27_out, and_28_out, and_29_out, and_30_out, and_31_out, and_32_out, and_33_out, and_34_out, and_35_out);
endmodule

// botoes controle
module botoes (
  input  ch2,
  input  ch1,
  input  ch0,
  input  elev_2,
  input  elev1,
  input  elev0,
  output ch_2,
  output ch1_2,
  output ch0_2,
  output b2,
  output b1,
  output b0
);

  wire clock_1_out;

  Clock clock_1 (.out(clock_1_out));
  D_Flip_Flop ch2FF (.Q(ch_2), .preset(ch2), .reset(clock_1_out));  // open: clk, D, Qn, en
  D_Flip_Flop CH1FF (.Q(ch1_2), .preset(ch1), .reset(clock_1_out));  // open: clk, D, Qn, en
  D_Flip_Flop CH0FF (.Q(ch0_2), .preset(ch0), .reset(clock_1_out));  // open: clk, D, Qn, en
  D_Flip_Flop B_2_FF (.Q(b2), .preset(elev_2), .reset(clock_1_out));  // open: clk, D, Qn, en
  D_Flip_Flop B1_FF (.Q(b1), .preset(elev1), .reset(clock_1_out));  // open: clk, D, Qn, en
  D_Flip_Flop B_0_FF (.Q(b0), .preset(elev0), .reset(clock_1_out));  // open: clk, D, Qn, en
endmodule

// elevador controle
module controle (
  input  b0,
  input  b1,
  input  b2,
  input  b3,
  input  b4,
  input  b5,
  output subindo,
  output _0_andar,
  output porta_aberta,
  output _1_andar,
  output pronto,
  output _2_andar,
  output porta_fechada,
  output descendo,
  output livre,
  output ocupado
);

  wire _1_andar_q, _2_andar_q, Clock_out, d_ff_1_q, d_ff_2_q, d_ff_3_q, d_ff_4_q, d_ff_5_q, d_ff_6_q,
       d_ff_7_q, d_ff_8_q, d_ff_9_q, d_ff_10_q, d_ff_11_q, d_ff_12_q, logica_1_parado_pronto, logica_1_porta,
       or_1_out, or_2_out, or_3_out, or_4_out, or_5_out, or_6_out, terreo_q;

  Clock Clock (.out(Clock_out));
  or or_1 (or_1_out, d_ff_1_q, d_ff_2_q);
  or or_2 (or_2_out, d_ff_3_q, d_ff_4_q);
  or or_3 (or_3_out, d_ff_5_q, d_ff_6_q);
  D_Flip_Flop terreo (.clk(Clock_out), .D(_0_andar), .Q(terreo_q));  // open: Qn, preset, en, reset
  D_Flip_Flop u__1_andar (.clk(Clock_out), .D(_1_andar), .Q(_1_andar_q));  // open: Qn, preset, en, reset
  D_Flip_Flop u__2_andar (.clk(Clock_out), .D(_2_andar), .Q(_2_andar_q));  // open: Qn, preset, en, reset
  D_Flip_Flop d_ff_1 (.clk(Clock_out), .D(d_ff_2_q), .Q(d_ff_1_q));  // open: Qn, preset, en, reset
  D_Flip_Flop d_ff_2 (.clk(Clock_out), .D(b0), .Q(d_ff_2_q));  // open: Qn, preset, en, reset
  D_Flip_Flop d_ff_3 (.clk(Clock_out), .D(d_ff_4_q), .Q(d_ff_3_q));  // open: Qn, preset, en, reset
  D_Flip_Flop d_ff_4 (.clk(Clock_out), .D(b2), .Q(d_ff_4_q));  // open: Qn, preset, en, reset
  D_Flip_Flop d_ff_5 (.clk(Clock_out), .D(d_ff_6_q), .Q(d_ff_5_q));  // open: Qn, preset, en, reset
  D_Flip_Flop d_ff_6 (.clk(Clock_out), .D(b4), .Q(d_ff_6_q));  // open: Qn, preset, en, reset
  D_Flip_Flop d_ff_7 (.clk(Clock_out), .D(d_ff_8_q), .Q(d_ff_7_q));  // open: Qn, preset, en, reset
  D_Flip_Flop d_ff_8 (.clk(Clock_out), .D(b1), .Q(d_ff_8_q));  // open: Qn, preset, en, reset
  D_Flip_Flop d_ff_9 (.clk(Clock_out), .D(d_ff_10_q), .Q(d_ff_9_q));  // open: Qn, preset, en, reset
  D_Flip_Flop d_ff_10 (.clk(Clock_out), .D(b3), .Q(d_ff_10_q));  // open: Qn, preset, en, reset
  D_Flip_Flop d_ff_11 (.clk(Clock_out), .D(d_ff_12_q), .Q(d_ff_11_q));  // open: Qn, preset, en, reset
  D_Flip_Flop d_ff_12 (.clk(Clock_out), .D(b5), .Q(d_ff_12_q));  // open: Qn, preset, en, reset
  or or_4 (or_4_out, d_ff_7_q, d_ff_8_q);
  or or_5 (or_5_out, d_ff_9_q, d_ff_10_q);
  or or_6 (or_6_out, d_ff_11_q, d_ff_12_q);
  logica logica_1 (
    .esta_no_terreo(terreo_q), .ch_1_andar_do_terreo(_1_andar_q), .ch_2_andar_do_terro(_2_andar_q),
    .ch_chamada_chao(or_1_out), .chamada1andar(or_4_out), .chamada2andar(or_2_out), ._0_elevaor(or_5_out),
    ._1_elevador(or_3_out), ._2_elevadr(or_6_out), .andar_0(_0_andar), .andar_1(_1_andar),
    .andar_2(_2_andar), .parado_pronto(logica_1_parado_pronto), .porta(logica_1_porta), .pra_cima(subindo),
    .pra_baixo(descendo));
  not not_1 (pronto, logica_1_parado_pronto);
  LED _0 (.in(_0_andar));
  LED _1 (.in(_1_andar));
  Decoder #(.enable("false")) decoder_1 (.out0(livre), .out1(ocupado), .sel(logica_1_parado_pronto));
  Decoder #(.enable("false")) decoder_2 (.out0(porta_aberta), .out1(porta_fechada), .sel(logica_1_porta));
  LED _2 (.in(_2_andar));
  LED led_1 (.in(subindo));
  LED led_2 (.in(pronto));
  LED led_3 (.in(descendo));
  LED led_4 (.in(porta_aberta));
  LED led_5 (.in(porta_fechada));
  LED led_6 (.in(livre));
  LED led_7 (.in(ocupado));

  // Notes on the sheet:
  //   acionador
  //   entradas dos botoes
endmodule

module elevador__main (
);

  wire _0__botao_elevador_out, _1__botao_elevador_out, _2__botao_elevador_out, botoes_1_b0, botoes_1_b1,
       botoes_1_b2, botoes_1_ch0_2, botoes_1_ch1_2, botoes_1_ch_2, chamada_1_andar_out, chamada_2_andar_out,
       chamada_terreo_out, controle_1__0_andar, controle_1__1_andar, controle_1__2_andar,
       controle_1_descendo, controle_1_livre, controle_1_ocupado, controle_1_porta_aberta,
       controle_1_porta_fechada, controle_1_pronto, controle_1_subindo, display_7_1_a, display_7_1_b,
       display_7_1_c, display_7_1_d, display_7_1_e, display_7_1_f, display_7_1_g, display_7_1_ponto;

  Button chamada_2_andar (.out(chamada_2_andar_out));
  Button chamada_1_andar (.out(chamada_1_andar_out));
  Button chamada_terreo (.out(chamada_terreo_out));
  Button _2__botao_elevador (.out(_2__botao_elevador_out));
  Button _1__botao_elevador (.out(_1__botao_elevador_out));
  Button _0__botao_elevador (.out(_0__botao_elevador_out));
  botoes botoes_1 (
    .ch2(_2__botao_elevador_out), .ch1(_1__botao_elevador_out), .ch0(_0__botao_elevador_out),
    .elev_2(chamada_2_andar_out), .elev1(chamada_1_andar_out), .elev0(chamada_terreo_out),
    .ch_2(botoes_1_ch_2), .ch1_2(botoes_1_ch1_2), .ch0_2(botoes_1_ch0_2), .b2(botoes_1_b2), .b1(botoes_1_b1),
    .b0(botoes_1_b0));
  LED livre (.in(controle_1_livre));
  controle controle_1 (
    .subindo(controle_1_subindo), ._0_andar(controle_1__0_andar), ._1_andar(controle_1__1_andar),
    .pronto(controle_1_pronto), ._2_andar(controle_1__2_andar), .descendo(controle_1_descendo),
    .ocupado(controle_1_ocupado), .b0(botoes_1_b0), .b1(botoes_1_b1), .b2(botoes_1_b2), .b3(botoes_1_ch0_2),
    .b4(botoes_1_ch1_2), .b5(botoes_1_ch_2), .porta_aberta(controle_1_porta_aberta),
    .porta_fechada(controle_1_porta_fechada), .livre(controle_1_livre));
  LED em_uso (.in(controle_1_ocupado));
  display_7 display_7_1 (
    .andar_0(controle_1__0_andar), .andar_1(controle_1__1_andar), .andar_2(controle_1__2_andar),
    .a(display_7_1_a), .b(display_7_1_b), .c(display_7_1_c), .d(display_7_1_d), .e(display_7_1_e),
    .f(display_7_1_f), .g(display_7_1_g), .ponto(display_7_1_ponto));
  _7_Segment_Display u_7_segment_display_1 (
    .g(display_7_1_g), .f(display_7_1_f), .a(display_7_1_a), .b(display_7_1_b), .e(display_7_1_e),
    .d(display_7_1_d), .c(display_7_1_c), .dp(display_7_1_ponto));
  LED porta_aberta (.in(controle_1_porta_aberta));
  LED Subindo (.in(controle_1_subindo));
  LED Parado (.in(controle_1_pronto));
  LED Descendo (.in(controle_1_descendo));
  LED porta_fechada (.in(controle_1_porta_fechada));
endmodule
