// Logisim project ULA LOGSIM.circ as structural Verilog: 11 circuits, main circuit CI Teste
module ULA (
  input  in_1,
  input  in_2,
  input  in_3,
  input  in_4,
  input  in_5,
  input  in_6,
  input  in_7,
  input  in_8,
  input  in_9,
  input  in_10,
  input  in_11,
  input  in_12,
  input  in_13,
  output out_14,
  output out_15,
  output out_16,
  output out_17,
  output out_18,
  output R_0,
  output OverFlow,
  output X___Y,
  output X___Y_2,
  output X___Y_3
);

  wire n2x_1_out_11, not_2_out, not_3_out, not_4_out, not_5_out, or_1_out, or_3_out, plus_1_out_16,
       sub_1_out_11, sub_1_out_12, sub_1_out_13, sub_1_out_14, sub_1_out_15, sub_2_out_16;
  wire [4:0] and_2_out_15, demultiplexer_1_out0, demultiplexer_1_out1, demultiplexer_1_out2,
       demultiplexer_1_out3, demultiplexer_1_out4, demultiplexer_1_out5, demultiplexer_2_out0,
       demultiplexer_2_out1, demultiplexer_2_out2, demultiplexer_2_out3, n2x_1_out_10, or_4_out_15,
       plus_1_out_15, sub_2_out_15, x_1_out_10;

  Demultiplexer #(.select(3), .width(5), .enable("false")) demultiplexer_1 (
    .out0(demultiplexer_1_out0), .out1(demultiplexer_1_out1), .out2(demultiplexer_1_out2),
    .out3(demultiplexer_1_out3), .out4(demultiplexer_1_out4), .out5(demultiplexer_1_out5),
    .in({in_1, in_2, in_3, in_4, in_5}), .sel({in_11, in_12, in_13}));  // open: out6, out7
  Demultiplexer #(.select(3), .width(5), .enable("false")) demultiplexer_2 (
    .out0(demultiplexer_2_out0), .out1(demultiplexer_2_out1), .out2(demultiplexer_2_out2),
    .out3(demultiplexer_2_out3), .in({in_6, in_7, in_8, in_9, in_10}), .sel({in_11, in_12, in_13}));  // open: out4, out5, out6, out7
  or or_1 (or_1_out, out_14, out_15, out_16, out_17, out_18);
  not not_1 (R_0, or_1_out);
  or or_2 (OverFlow, plus_1_out_16, sub_2_out_16, n2x_1_out_11);
  not not_2 (not_2_out, X___Y_2);
  assign X___Y = not_4_out ? not_2_out : 1'bz;  // Controlled_Buffer controlled_buffer_1
  Sub sub_1 (
    ._4A(in_1), ._3A(in_2), ._2A(in_3), ._1A(in_4), ._0A(in_5), .in_6(in_6), .in_7(in_7), .in_8(in_8),
    .in_9(in_9), .in_10(in_10), .out_11(sub_1_out_11), .out_12(sub_1_out_12), .out_13(sub_1_out_13),
    .out_14(sub_1_out_14), .out_15(sub_1_out_15), .out_16(X___Y_2));
  not not_3 (not_3_out, X___Y_2);
  not not_4 (not_4_out, X___Y_3);
  or or_3 (or_3_out, sub_1_out_15, sub_1_out_14, sub_1_out_13, sub_1_out_12, sub_1_out_11);
  not not_5 (not_5_out, or_3_out);
  and and_1 (X___Y_3, not_3_out, not_5_out);
  Plus plus_1 (
    ._4A(demultiplexer_1_out0[4]), ._3A(demultiplexer_1_out0[3]), ._2A(demultiplexer_1_out0[2]),
    ._1A(demultiplexer_1_out0[1]), ._0A(demultiplexer_1_out0[0]), .in_6(demultiplexer_2_out0[4]),
    .in_7(demultiplexer_2_out0[3]), .in_8(demultiplexer_2_out0[2]), .in_9(demultiplexer_2_out0[1]),
    .in_10(demultiplexer_2_out0[0]), .out_11(plus_1_out_15[4]), .out_12(plus_1_out_15[3]),
    .out_13(plus_1_out_15[2]), .out_14(plus_1_out_15[1]), .out_15(plus_1_out_15[0]), .out_16(plus_1_out_16));
  Sub sub_2 (
    ._4A(demultiplexer_1_out1[4]), ._3A(demultiplexer_1_out1[3]), ._2A(demultiplexer_1_out1[2]),
    ._1A(demultiplexer_1_out1[1]), ._0A(demultiplexer_1_out1[0]), .in_6(demultiplexer_2_out1[4]),
    .in_7(demultiplexer_2_out1[3]), .in_8(demultiplexer_2_out1[2]), .in_9(demultiplexer_2_out1[1]),
    .in_10(demultiplexer_2_out1[0]), .out_11(sub_2_out_15[4]), .out_12(sub_2_out_15[3]),
    .out_13(sub_2_out_15[2]), .out_14(sub_2_out_15[1]), .out_15(sub_2_out_15[0]), .out_16(sub_2_out_16));
  AND and_2 (
    ._4A(demultiplexer_1_out2[4]), ._3A(demultiplexer_1_out2[3]), ._2A(demultiplexer_1_out2[2]),
    ._1A(demultiplexer_1_out2[1]), ._0A(demultiplexer_1_out2[0]), .in_6(demultiplexer_2_out2[4]),
    .in_7(demultiplexer_2_out2[3]), .in_8(demultiplexer_2_out2[2]), .in_9(demultiplexer_2_out2[1]),
    .in_10(demultiplexer_2_out2[0]), .out_11(and_2_out_15[4]), .out_12(and_2_out_15[3]),
    .out_13(and_2_out_15[2]), .out_14(and_2_out_15[1]), .out_15(and_2_out_15[0]));
  OR or_4 (
    ._4A(demultiplexer_1_out3[4]), ._3A(demultiplexer_1_out3[3]), ._2A(demultiplexer_1_out3[2]),
    ._1A(demultiplexer_1_out3[1]), ._0A(demultiplexer_1_out3[0]), .in_6(demultiplexer_2_out3[4]),
    .in_7(demultiplexer_2_out3[3]), .in_8(demultiplexer_2_out3[2]), .in_9(demultiplexer_2_out3[1]),
    .in_10(demultiplexer_2_out3[0]), .out_11(or_4_out_15[4]), .out_12(or_4_out_15[3]),
    .out_13(or_4_out_15[2]), .out_14(or_4_out_15[1]), .out_15(or_4_out_15[0]));
  X x_1 (
    ._4A(demultiplexer_1_out4[4]), ._3A(demultiplexer_1_out4[3]), ._2A(demultiplexer_1_out4[2]),
    ._1A(demultiplexer_1_out4[1]), ._0A(demultiplexer_1_out4[0]), .out_6(x_1_out_10[4]),
    .out_7(x_1_out_10[3]), .out_8(x_1_out_10[2]), .out_9(x_1_out_10[1]), .out_10(x_1_out_10[0]));
  _2X u_2x_1 (
    ._4A(demultiplexer_1_out5[4]), ._3A(demultiplexer_1_out5[3]), ._2A(demultiplexer_1_out5[2]),
    ._1A(demultiplexer_1_out5[1]), ._0A(demultiplexer_1_out5[0]), .out_6(n2x_1_out_10[4]),
    .out_7(n2x_1_out_10[3]), .out_8(n2x_1_out_10[2]), .out_9(n2x_1_out_10[1]), .out_10(n2x_1_out_10[0]),
    .out_11(n2x_1_out_11));
  Multiplexer #(.select(3), .width(5), .enable("false")) multiplexer_1 (
    .in0(plus_1_out_15), .in1(sub_2_out_15), .in2(and_2_out_15), .in3(or_4_out_15), .in4(x_1_out_10),
    .in5(n2x_1_out_10), .in6({in_1, in_2, in_3, in_4, in_5}), .in7({in_6, in_7, in_8, in_9, in_10}),
    .out({out_14, out_15, out_16, out_17, out_18}), .sel({in_11, in_12, in_13}));
endmodule

module Plus (
  input  _4A,
  input  _3A,
  input  _2A,
  input  _1A,
  input  _0A,
  input  in_6,
  input  in_7,
  input  in_8,
  input  in_9,
  input  in_10,
  output out_11,
  output out_12,
  output out_13,
  output out_14,
  output out_15,
  output out_16
);

  wire adder_1_cout, adder_2_cout, adder_3_cout, adder_4_cout, not_1_out;

  not not_1 (not_1_out, 1'b1);
  Adder #(.width(1)) adder_1 (.a(_0A), .b(in_10), .out(out_15), .cin(not_1_out), .cout(adder_1_cout));
  Adder #(.width(1)) adder_2 (.a(_1A), .b(in_9), .out(out_14), .cin(adder_1_cout), .cout(adder_2_cout));
  Adder #(.width(1)) adder_3 (.a(_2A), .b(in_8), .out(out_13), .cin(adder_2_cout), .cout(adder_3_cout));
  Adder #(.width(1)) adder_4 (.a(_3A), .b(in_7), .out(out_12), .cin(adder_3_cout), .cout(adder_4_cout));
  Adder #(.width(1)) adder_5 (.a(_4A), .b(in_6), .out(out_11), .cin(adder_4_cout), .cout(out_16));
endmodule

module Sub (
  input  _4A,
  input  _3A,
  input  _2A,
  input  _1A,
  input  _0A,
  input  in_6,
  input  in_7,
  input  in_8,
  input  in_9,
  input  in_10,
  output out_11,
  output out_12,
  output out_13,
  output out_14,
  output out_15,
  output out_16
);

  wire not_1_out, subtractor_1_bout, subtractor_2_bout, subtractor_3_bout, subtractor_4_bout;

  not not_1 (not_1_out, 1'b1);
  Subtractor #(.width(1)) subtractor_1 (.a(_0A), .b(in_10), .out(out_15), .bin(not_1_out), .bout(subtractor_1_bout));
  Subtractor #(.width(1)) subtractor_2 (
    .a(_1A), .b(in_9), .out(out_14), .bin(subtractor_1_bout), .bout(subtractor_2_bout));
  Subtractor #(.width(1)) subtractor_3 (
    .a(_2A), .b(in_8), .out(out_13), .bin(subtractor_2_bout), .bout(subtractor_3_bout));
  Subtractor #(.width(1)) subtractor_4 (
    .a(_3A), .b(in_7), .out(out_12), .bin(subtractor_3_bout), .bout(subtractor_4_bout));
  Subtractor #(.width(1)) subtractor_5 (.a(_4A), .b(in_6), .out(out_11), .bin(subtractor_4_bout), .bout(out_16));
endmodule

module AND (
  input  _4A,
  input  _3A,
  input  _2A,
  input  _1A,
  input  _0A,
  input  in_6,
  input  in_7,
  input  in_8,
  input  in_9,
  input  in_10,
  output out_11,
  output out_12,
  output out_13,
  output out_14,
  output out_15
);

  and and_1 (out_15, _0A, in_10);
  and and_2 (out_14, _1A, in_9);
  and and_3 (out_13, _2A, in_8);
  and and_4 (out_12, _3A, in_7);
  and and_5 (out_11, _4A, in_6);
endmodule

module OR (
  input  _4A,
  input  _3A,
  input  _2A,
  input  _1A,
  input  _0A,
  input  in_6,
  input  in_7,
  input  in_8,
  input  in_9,
  input  in_10,
  output out_11,
  output out_12,
  output out_13,
  output out_14,
  output out_15
);

  or or_1 (out_15, _0A, in_10);
  or or_2 (out_14, _1A, in_9);
  or or_3 (out_13, _2A, in_8);
  or or_4 (out_12, _3A, in_7);
  or or_5 (out_11, _4A, in_6);
endmodule

module X (
  input  _4A,
  input  _3A,
  input  _2A,
  input  _1A,
  input  _0A,
  output out_6,
  output out_7,
  output out_8,
  output out_9,
  output out_10
);

  not not_1 (out_10, _0A);
  not not_2 (out_9, _1A);
  not not_3 (out_8, _2A);
  not not_4 (out_7, _3A);
  not not_5 (out_6, _4A);
endmodule

module _2X (
  input  _4A,
  input  _3A,
  input  _2A,
  input  _1A,
  input  _0A,
  output out_6,
  output out_7,
  output out_8,
  output out_9,
  output out_10,
  output out_11
);

  wire adder_1_cout, adder_2_cout, adder_3_cout, adder_4_cout, not_1_out;

  not not_1 (not_1_out, 1'b1);
  Adder #(.width(1)) adder_1 (.a(_0A), .b(_0A), .out(out_10), .cin(not_1_out), .cout(adder_1_cout));
  Adder #(.width(1)) adder_2 (.a(_1A), .b(_1A), .out(out_9), .cin(adder_1_cout), .cout(adder_2_cout));
  Adder #(.width(1)) adder_3 (.a(_2A), .b(_2A), .out(out_8), .cin(adder_2_cout), .cout(adder_3_cout));
  Adder #(.width(1)) adder_4 (.a(_3A), .b(_3A), .out(out_7), .cin(adder_3_cout), .cout(adder_4_cout));
  Adder #(.width(1)) adder_5 (.a(_4A), .b(_4A), .out(out_6), .cin(adder_4_cout), .cout(out_11));
endmodule

module CI_Teste (
  input  [4:0] A,
  input  [2:0] SELECT,
  input  [4:0] B
);

  wire n7_seg_mais_sig_1_a_2, n7_seg_mais_sig_1_b_2, n7_seg_mais_sig_1_c_2, n7_seg_mais_sig_1_d_2,
       n7_seg_mais_sig_1_e_2, n7_seg_mais_sig_1_f, n7_seg_mais_sig_1_g, n7_seg_mais_sig_2_a_2,
       n7_seg_mais_sig_2_b_2, n7_seg_mais_sig_2_c_2, n7_seg_mais_sig_2_d_2, n7_seg_mais_sig_2_e_2,
       n7_seg_mais_sig_2_f, n7_seg_mais_sig_2_g, n7_seg_mais_sig_3_a_2, n7_seg_mais_sig_3_b_2,
       n7_seg_mais_sig_3_c_2, n7_seg_mais_sig_3_d_2, n7_seg_mais_sig_3_e_2, n7_seg_mais_sig_3_f,
       n7_seg_mais_sig_3_g, n7_seg_menos_sig_1_a_2, n7_seg_menos_sig_1_b_2, n7_seg_menos_sig_1_c_2,
       n7_seg_menos_sig_1_d_2, n7_seg_menos_sig_1_e_2, n7_seg_menos_sig_1_f, n7_seg_menos_sig_1_g,
       n7_seg_menos_sig_2_a_2, n7_seg_menos_sig_2_b_2, n7_seg_menos_sig_2_c_2, n7_seg_menos_sig_2_d_2,
       n7_seg_menos_sig_2_e_2, n7_seg_menos_sig_2_f, n7_seg_menos_sig_2_g, n7_seg_menos_sig_3_a_2,
       n7_seg_menos_sig_3_b_2, n7_seg_menos_sig_3_c_2, n7_seg_menos_sig_3_d_2, n7_seg_menos_sig_3_e_2,
       n7_seg_menos_sig_3_f, n7_seg_menos_sig_3_g, ula_1_overflow, ula_1_r_0, ula_1_x___y, ula_1_x___y_2,
       ula_1_x___y_3;
  wire [4:0] led_5x5_1_out_2, led_5x5_1_out_3, led_5x5_1_out_4, led_5x5_1_out_5, led_5x5_1_out_6,
       ula_1_out_18;

  _7_seg_mais_sig u_7_seg_mais_sig_1 (
    .A(A[4]), .B(A[3]), .C(A[2]), .D(A[1]), .E(A[0]), .a_2(n7_seg_mais_sig_1_a_2),
    .b_2(n7_seg_mais_sig_1_b_2), .c_2(n7_seg_mais_sig_1_c_2), .d_2(n7_seg_mais_sig_1_d_2),
    .e_2(n7_seg_mais_sig_1_e_2), .f(n7_seg_mais_sig_1_f), .g(n7_seg_mais_sig_1_g));
  _7_seg_MENOS_SIG u_7_seg_menos_sig_1 (
    .A(A[4]), .B(A[3]), .C(A[2]), .D(A[1]), .E(A[0]), .a_2(n7_seg_menos_sig_1_a_2),
    .b_2(n7_seg_menos_sig_1_b_2), .c_2(n7_seg_menos_sig_1_c_2), .d_2(n7_seg_menos_sig_1_d_2),
    .e_2(n7_seg_menos_sig_1_e_2), .f(n7_seg_menos_sig_1_f), .g(n7_seg_menos_sig_1_g));
  _7_Segment_Display u_7_segment_display_1 (
    .g(n7_seg_mais_sig_1_g), .f(n7_seg_mais_sig_1_f), .a(n7_seg_mais_sig_1_a_2), .b(n7_seg_mais_sig_1_b_2),
    .e(n7_seg_mais_sig_1_e_2), .d(n7_seg_mais_sig_1_d_2), .c(n7_seg_mais_sig_1_c_2));  // open: dp
  _7_seg_mais_sig u_7_seg_mais_sig_2 (
    .A(B[4]), .B(B[3]), .C(B[2]), .D(B[1]), .E(B[0]), .a_2(n7_seg_mais_sig_2_a_2),
    .b_2(n7_seg_mais_sig_2_b_2), .c_2(n7_seg_mais_sig_2_c_2), .d_2(n7_seg_mais_sig_2_d_2),
    .e_2(n7_seg_mais_sig_2_e_2), .f(n7_seg_mais_sig_2_f), .g(n7_seg_mais_sig_2_g));
  _7_seg_MENOS_SIG u_7_seg_menos_sig_2 (
    .A(B[4]), .B(B[3]), .C(B[2]), .D(B[1]), .E(B[0]), .a_2(n7_seg_menos_sig_2_a_2),
    .b_2(n7_seg_menos_sig_2_b_2), .c_2(n7_seg_menos_sig_2_c_2), .d_2(n7_seg_menos_sig_2_d_2),
    .e_2(n7_seg_menos_sig_2_e_2), .f(n7_seg_menos_sig_2_f), .g(n7_seg_menos_sig_2_g));
  _7_Segment_Display u_7_segment_display_2 (
    .g(n7_seg_menos_sig_1_g), .f(n7_seg_menos_sig_1_f), .a(n7_seg_menos_sig_1_a_2),
    .b(n7_seg_menos_sig_1_b_2), .e(n7_seg_menos_sig_1_e_2), .d(n7_seg_menos_sig_1_d_2),
    .c(n7_seg_menos_sig_1_c_2));  // open: dp
  _7_Segment_Display u_7_segment_display_3 (
    .g(n7_seg_mais_sig_2_g), .f(n7_seg_mais_sig_2_f), .a(n7_seg_mais_sig_2_a_2), .b(n7_seg_mais_sig_2_b_2),
    .e(n7_seg_mais_sig_2_e_2), .d(n7_seg_mais_sig_2_d_2), .c(n7_seg_mais_sig_2_c_2));  // open: dp
  _7_Segment_Display u_7_segment_display_4 (
    .g(n7_seg_menos_sig_2_g), .f(n7_seg_menos_sig_2_f), .a(n7_seg_menos_sig_2_a_2),
    .b(n7_seg_menos_sig_2_b_2), .e(n7_seg_menos_sig_2_e_2), .d(n7_seg_menos_sig_2_d_2),
    .c(n7_seg_menos_sig_2_c_2));  // open: dp
  Led_5x5 led_5x5_1 (
    .in_1(SELECT), .out_2(led_5x5_1_out_2), .out_3(led_5x5_1_out_3), .out_4(led_5x5_1_out_4),
    .out_5(led_5x5_1_out_5), .out_6(led_5x5_1_out_6));
  LED led_1 (.in(ula_1_r_0));
  ULA ula_1 (
    .in_1(A[4]), .in_2(A[3]), .in_3(A[2]), .in_4(A[1]), .in_5(A[0]), .in_6(B[4]), .in_7(B[3]), .in_8(B[2]),
    .in_9(B[1]), .in_10(B[0]), .out_14(ula_1_out_18[4]), .out_15(ula_1_out_18[3]), .out_16(ula_1_out_18[2]),
    .out_17(ula_1_out_18[1]), .out_18(ula_1_out_18[0]), .OverFlow(ula_1_overflow), .R_0(ula_1_r_0),
    .X___Y(ula_1_x___y), .X___Y_2(ula_1_x___y_2), .X___Y_3(ula_1_x___y_3), .in_12(SELECT[1]),
    .in_13(SELECT[0]), .in_11(SELECT[2]));
  LED led_2 (.in(ula_1_overflow));
  DotMatrix #(.inputtype("row"), .matrixrows(5)) dotmatrix_1 (
    .row0(led_5x5_1_out_2), .row1(led_5x5_1_out_3), .row2(led_5x5_1_out_4), .row3(led_5x5_1_out_5),
    .row4(led_5x5_1_out_6));
  LED led_3 (.in(ula_1_x___y));
  LED led_4 (.in(ula_1_x___y_2));
  LED led_5 (.in(ula_1_x___y_3));
  _7_seg_mais_sig u_7_seg_mais_sig_3 (
    .A(ula_1_out_18[4]), .B(ula_1_out_18[3]), .C(ula_1_out_18[2]), .D(ula_1_out_18[1]), .E(ula_1_out_18[0]),
    .a_2(n7_seg_mais_sig_3_a_2), .b_2(n7_seg_mais_sig_3_b_2), .c_2(n7_seg_mais_sig_3_c_2),
    .d_2(n7_seg_mais_sig_3_d_2), .e_2(n7_seg_mais_sig_3_e_2), .f(n7_seg_mais_sig_3_f), .g(n7_seg_mais_sig_3_g));
  _7_seg_MENOS_SIG u_7_seg_menos_sig_3 (
    .A(ula_1_out_18[4]), .B(ula_1_out_18[3]), .C(ula_1_out_18[2]), .D(ula_1_out_18[1]), .E(ula_1_out_18[0]),
    .a_2(n7_seg_menos_sig_3_a_2), .b_2(n7_seg_menos_sig_3_b_2), .c_2(n7_seg_menos_sig_3_c_2),
    .d_2(n7_seg_menos_sig_3_d_2), .e_2(n7_seg_menos_sig_3_e_2), .f(n7_seg_menos_sig_3_f),
    .g(n7_seg_menos_sig_3_g));
  _7_Segment_Display u_7_segment_display_5 (
    .g(n7_seg_mais_sig_3_g), .f(n7_seg_mais_sig_3_f), .a(n7_seg_mais_sig_3_a_2), .b(n7_seg_mais_sig_3_b_2),
    .e(n7_seg_mais_sig_3_e_2), .d(n7_seg_mais_sig_3_d_2), .c(n7_seg_mais_sig_3_c_2));  // open: dp
  _7_Segment_Display u_7_segment_display_6 (
    .g(n7_seg_menos_sig_3_g), .f(n7_seg_menos_sig_3_f), .a(n7_seg_menos_sig_3_a_2),
    .b(n7_seg_menos_sig_3_b_2), .e(n7_seg_menos_sig_3_e_2), .d(n7_seg_menos_sig_3_d_2),
    .c(n7_seg_menos_sig_3_c_2));  // open: dp

  // Notes on the sheet:
  //   A
  //   B
  //   R=0
  //   OverFlow
  //   X > Y
  //   X < Y
  //   X = Y
endmodule

module Led_5x5 (
  input  [2:0] in_1,
  output [4:0] out_2,
  output [4:0] out_3,
  output [4:0] out_4,
  output [4:0] out_5,
  output [4:0] out_6
);

  wire decoder_1_out0, decoder_1_out1, decoder_1_out2, decoder_1_out3, decoder_1_out4, decoder_1_out5,
       decoder_1_out6, decoder_1_out7;
  wire [4:0] controlled_buffer_1_out, controlled_buffer_2_out, controlled_buffer_3_out,
       controlled_buffer_4_out, controlled_buffer_5_out, controlled_buffer_6_out, controlled_buffer_7_out,
       controlled_buffer_8_out, controlled_buffer_9_out, controlled_buffer_10_out, controlled_buffer_11_out,
       controlled_buffer_12_out, controlled_buffer_13_out, controlled_buffer_14_out,
       controlled_buffer_15_out, controlled_buffer_16_out, controlled_buffer_17_out,
       controlled_buffer_18_out, controlled_buffer_19_out, controlled_buffer_20_out,
       controlled_buffer_21_out, controlled_buffer_22_out, controlled_buffer_23_out,
       controlled_buffer_24_out, controlled_buffer_25_out, controlled_buffer_26_out,
       controlled_buffer_27_out, controlled_buffer_28_out, controlled_buffer_29_out,
       controlled_buffer_30_out, controlled_buffer_31_out, controlled_buffer_32_out,
       controlled_buffer_33_out, controlled_buffer_34_out, controlled_buffer_35_out,
       controlled_buffer_36_out, controlled_buffer_37_out, controlled_buffer_38_out,
       controlled_buffer_39_out, controlled_buffer_40_out;

  Decoder #(.select(3), .enable("false")) decoder_1 (
    .out0(decoder_1_out0), .out1(decoder_1_out1), .out2(decoder_1_out2), .out3(decoder_1_out3),
    .out4(decoder_1_out4), .out5(decoder_1_out5), .out6(decoder_1_out6), .out7(decoder_1_out7), .sel(in_1));
  assign controlled_buffer_1_out = decoder_1_out0 ? 5'b00100 : 5'bz;  // Controlled_Buffer controlled_buffer_1
  assign controlled_buffer_2_out = decoder_1_out1 ? {5{1'b0}} : 5'bz;  // Controlled_Buffer controlled_buffer_2
  assign controlled_buffer_3_out = decoder_1_out2 ? {5{1'b1}} : 5'bz;  // Controlled_Buffer controlled_buffer_3
  assign controlled_buffer_4_out = decoder_1_out3 ? {5{1'b1}} : 5'bz;  // Controlled_Buffer controlled_buffer_4
  assign controlled_buffer_5_out = decoder_1_out4 ? 5'b10001 : 5'bz;  // Controlled_Buffer controlled_buffer_5
  assign controlled_buffer_6_out = decoder_1_out5 ? {5{1'b1}} : 5'bz;  // Controlled_Buffer controlled_buffer_6
  assign controlled_buffer_7_out = decoder_1_out6 ? 5'b10001 : 5'bz;  // Controlled_Buffer controlled_buffer_7
  assign controlled_buffer_8_out = decoder_1_out7 ? 5'b10001 : 5'bz;  // Controlled_Buffer controlled_buffer_8
  assign controlled_buffer_9_out = decoder_1_out0 ? 5'b00100 : 5'bz;  // Controlled_Buffer controlled_buffer_9
  assign controlled_buffer_10_out = decoder_1_out0 ? {5{1'b1}} : 5'bz;  // Controlled_Buffer controlled_buffer_10
  assign controlled_buffer_11_out = decoder_1_out0 ? 5'b00100 : 5'bz;  // Controlled_Buffer controlled_buffer_11
  assign controlled_buffer_12_out = decoder_1_out0 ? 5'b00100 : 5'bz;  // Controlled_Buffer controlled_buffer_12
  assign controlled_buffer_13_out = decoder_1_out1 ? {5{1'b0}} : 5'bz;  // Controlled_Buffer controlled_buffer_13
  assign controlled_buffer_14_out = decoder_1_out1 ? {5{1'b1}} : 5'bz;  // Controlled_Buffer controlled_buffer_14
  assign controlled_buffer_15_out = decoder_1_out1 ? {5{1'b0}} : 5'bz;  // Controlled_Buffer controlled_buffer_15
  assign controlled_buffer_16_out = decoder_1_out1 ? {5{1'b0}} : 5'bz;  // Controlled_Buffer controlled_buffer_16
  assign controlled_buffer_17_out = decoder_1_out2 ? 5'b10001 : 5'bz;  // Controlled_Buffer controlled_buffer_17
  assign controlled_buffer_18_out = decoder_1_out2 ? {5{1'b1}} : 5'bz;  // Controlled_Buffer controlled_buffer_18
  assign controlled_buffer_19_out = decoder_1_out2 ? 5'b10001 : 5'bz;  // Controlled_Buffer controlled_buffer_19
  assign controlled_buffer_20_out = decoder_1_out2 ? 5'b10001 : 5'bz;  // Controlled_Buffer controlled_buffer_20
  assign controlled_buffer_21_out = decoder_1_out3 ? 5'b10001 : 5'bz;  // Controlled_Buffer controlled_buffer_21
  assign controlled_buffer_22_out = decoder_1_out3 ? 5'b10001 : 5'bz;  // Controlled_Buffer controlled_buffer_22
  assign controlled_buffer_23_out = decoder_1_out3 ? 5'b10001 : 5'bz;  // Controlled_Buffer controlled_buffer_23
  assign controlled_buffer_24_out = decoder_1_out3 ? {5{1'b1}} : 5'bz;  // Controlled_Buffer controlled_buffer_24
  assign controlled_buffer_25_out = decoder_1_out4 ? 5'b11001 : 5'bz;  // Controlled_Buffer controlled_buffer_25
  assign controlled_buffer_26_out = decoder_1_out4 ? 5'b10101 : 5'bz;  // Controlled_Buffer controlled_buffer_26
  assign controlled_buffer_27_out = decoder_1_out4 ? 5'b10011 : 5'bz;  // Controlled_Buffer controlled_buffer_27
  assign controlled_buffer_28_out = decoder_1_out4 ? 5'b10001 : 5'bz;  // Controlled_Buffer controlled_buffer_28
  assign controlled_buffer_29_out = decoder_1_out5 ? 5'b00001 : 5'bz;  // Controlled_Buffer controlled_buffer_29
  assign controlled_buffer_30_out = decoder_1_out5 ? {5{1'b1}} : 5'bz;  // Controlled_Buffer controlled_buffer_30
  assign controlled_buffer_31_out = decoder_1_out5 ? 5'b10000 : 5'bz;  // Controlled_Buffer controlled_buffer_31
  assign controlled_buffer_32_out = decoder_1_out5 ? {5{1'b1}} : 5'bz;  // Controlled_Buffer controlled_buffer_32
  assign controlled_buffer_33_out = decoder_1_out6 ? 5'b01010 : 5'bz;  // Controlled_Buffer controlled_buffer_33
  assign controlled_buffer_34_out = decoder_1_out6 ? 5'b00100 : 5'bz;  // Controlled_Buffer controlled_buffer_34
  assign controlled_buffer_35_out = decoder_1_out6 ? 5'b01010 : 5'bz;  // Controlled_Buffer controlled_buffer_35
  assign controlled_buffer_36_out = decoder_1_out6 ? 5'b10001 : 5'bz;  // Controlled_Buffer controlled_buffer_36
  assign controlled_buffer_37_out = decoder_1_out7 ? 5'b01010 : 5'bz;  // Controlled_Buffer controlled_buffer_37
  assign controlled_buffer_38_out = decoder_1_out7 ? 5'b00100 : 5'bz;  // Controlled_Buffer controlled_buffer_38
  assign controlled_buffer_39_out = decoder_1_out7 ? 5'b00100 : 5'bz;  // Controlled_Buffer controlled_buffer_39
  assign controlled_buffer_40_out = decoder_1_out7 ? 5'b00100 : 5'bz;  // Controlled_Buffer controlled_buffer_40
  Multiplexer #(.select(3), .width(25), .enable("false")) multiplexer_1 (
    .in0({controlled_buffer_12_out, controlled_buffer_11_out, controlled_buffer_10_out, controlled_buffer_9_out, controlled_buffer_1_out}),
    .in1({controlled_buffer_16_out, controlled_buffer_15_out, controlled_buffer_14_out, controlled_buffer_13_out, controlled_buffer_2_out}),
    .in2({controlled_buffer_20_out, controlled_buffer_19_out, controlled_buffer_18_out, controlled_buffer_17_out, controlled_buffer_3_out}),
    .in3({controlled_buffer_24_out, controlled_buffer_23_out, controlled_buffer_22_out, controlled_buffer_21_out, controlled_buffer_4_out}),
    .in4({controlled_buffer_28_out, controlled_buffer_27_out, controlled_buffer_26_out, controlled_buffer_25_out, controlled_buffer_5_out}),
    .in5({controlled_buffer_32_out, controlled_buffer_31_out, controlled_buffer_30_out, controlled_buffer_29_out, controlled_buffer_6_out}),
    .in6({controlled_buffer_36_out, controlled_buffer_35_out, controlled_buffer_34_out, controlled_buffer_33_out, controlled_buffer_7_out}),
    .in7({controlled_buffer_40_out, controlled_buffer_39_out, controlled_buffer_38_out, controlled_buffer_37_out, controlled_buffer_8_out}),
    .out({out_6, out_5, out_4, out_3, out_2}), .sel(in_1));
endmodule

// 7 seg menos-sig
module _7_seg_MENOS_SIG (
  input  A,
  input  B,
  input  C,
  input  D,
  input  E,
  output a_2,
  output b_2,
  output c_2,
  output d_2,
  output e_2,
  output f,
  output g
);

  wire and_1_out, and_2_out, and_3_out, and_4_out, and_5_out, and_6_out, and_7_out, and_8_out, and_9_out,
       and_10_out, and_11_out, and_12_out, and_13_out, and_14_out, and_15_out, and_16_out, and_17_out,
       and_18_out, and_19_out, and_20_out, and_21_out, and_22_out, and_23_out, and_24_out, and_25_out,
       and_26_out, and_27_out, and_28_out, and_29_out, and_30_out, and_31_out, and_32_out, and_33_out,
       and_34_out, and_35_out, and_36_out, and_37_out, and_38_out, and_39_out, and_40_out, and_41_out,
       and_42_out, and_43_out, and_44_out, and_45_out, and_46_out, and_47_out, and_48_out, and_49_out,
       and_50_out, and_51_out, and_52_out, and_53_out, and_54_out, and_55_out, and_56_out, not_1_out,
       not_2_out, not_3_out, not_4_out, not_5_out, not_6_out, not_7_out, not_8_out, not_9_out, not_10_out,
       not_11_out, not_12_out, not_13_out, not_14_out, not_15_out, not_16_out, not_17_out, not_18_out,
       not_19_out, not_20_out, not_21_out, not_22_out, not_23_out, not_24_out, not_25_out, not_26_out,
       not_27_out, not_28_out, not_29_out, not_30_out, not_31_out, not_32_out, not_33_out, not_34_out,
       not_35_out, not_36_out, not_37_out, not_38_out, not_39_out, not_40_out, not_41_out, not_42_out,
       not_43_out, not_44_out, not_45_out, not_46_out, not_47_out, not_48_out, not_49_out, not_50_out,
       not_51_out, not_52_out, not_53_out, not_54_out, not_55_out, not_56_out, not_57_out, not_58_out,
       not_59_out, not_60_out, not_61_out, not_62_out, not_63_out, not_64_out, not_65_out, not_66_out,
       not_67_out, not_68_out, not_69_out, not_70_out, not_71_out, not_72_out, not_73_out, not_74_out,
       not_75_out, not_76_out, not_77_out, not_78_out, not_79_out, not_80_out, not_81_out, not_82_out,
       not_83_out, not_84_out, not_85_out, not_86_out, not_87_out, not_88_out, not_89_out, not_90_out,
       not_91_out, not_92_out, not_93_out, not_94_out, not_95_out, not_96_out, not_97_out, not_98_out,
       not_99_out, not_100_out, not_101_out;

  not not_1 (not_1_out, A);
  not not_2 (not_2_out, C);
  not not_3 (not_3_out, E);
  not not_4 (not_4_out, B);
  not not_5 (not_5_out, A);
  not not_6 (not_6_out, A);
  not not_7 (not_7_out, D);
  not not_8 (not_8_out, D);
  not not_9 (not_9_out, B);
  not not_10 (not_10_out, E);
  not not_11 (not_11_out, C);
  not not_12 (not_12_out, E);
  not not_13 (not_13_out, A);
  not not_14 (not_14_out, C);
  not not_15 (not_15_out, A);
  not not_16 (not_16_out, D);
  not not_17 (not_17_out, E);
  not not_18 (not_18_out, B);
  not not_19 (not_19_out, C);
  not not_20 (not_20_out, B);
  not not_21 (not_21_out, C);
  not not_22 (not_22_out, B);
  not not_23 (not_23_out, C);
  not not_24 (not_24_out, A);
  not not_25 (not_25_out, D);
  not not_26 (not_26_out, A);
  not not_27 (not_27_out, E);
  not not_28 (not_28_out, D);
  not not_29 (not_29_out, E);
  not not_30 (not_30_out, B);
  not not_31 (not_31_out, D);
  not not_32 (not_32_out, C);
  not not_33 (not_33_out, D);
  not not_34 (not_34_out, A);
  not not_35 (not_35_out, B);
  not not_36 (not_36_out, C);
  not not_37 (not_37_out, D);
  not not_38 (not_38_out, A);
  not not_39 (not_39_out, C);
  not not_40 (not_40_out, E);
  not not_41 (not_41_out, B);
  not not_42 (not_42_out, C);
  not not_43 (not_43_out, E);
  not not_44 (not_44_out, A);
  not not_45 (not_45_out, B);
  not not_46 (not_46_out, C);
  not not_47 (not_47_out, B);
  not not_48 (not_48_out, E);
  not not_49 (not_49_out, C);
  not not_50 (not_50_out, E);
  not not_51 (not_51_out, A);
  not not_52 (not_52_out, D);
  not not_53 (not_53_out, A);
  not not_54 (not_54_out, D);
  not not_55 (not_55_out, E);
  not not_56 (not_56_out, A);
  not not_57 (not_57_out, E);
  not not_58 (not_58_out, B);
  not not_59 (not_59_out, C);
  not not_60 (not_60_out, D);
  not not_61 (not_61_out, A);
  not not_62 (not_62_out, C);
  not not_63 (not_63_out, E);
  not not_64 (not_64_out, B);
  not not_65 (not_65_out, C);
  not not_66 (not_66_out, E);
  not not_67 (not_67_out, B);
  not not_68 (not_68_out, E);
  not not_69 (not_69_out, C);
  not not_70 (not_70_out, E);
  not not_71 (not_71_out, A);
  not not_72 (not_72_out, D);
  not not_73 (not_73_out, E);
  not not_74 (not_74_out, E);
  not not_75 (not_75_out, B);
  not not_76 (not_76_out, D);
  not not_77 (not_77_out, E);
  not not_78 (not_78_out, A);
  not not_79 (not_79_out, B);
  not not_80 (not_80_out, D);
  not not_81 (not_81_out, A);
  not not_82 (not_82_out, B);
  not not_83 (not_83_out, E);
  not not_84 (not_84_out, C);
  not not_85 (not_85_out, D);
  not not_86 (not_86_out, E);
  not not_87 (not_87_out, A);
  not not_88 (not_88_out, B);
  not not_89 (not_89_out, C);
  not not_90 (not_90_out, D);
  not not_91 (not_91_out, B);
  not not_92 (not_92_out, C);
  not not_93 (not_93_out, B);
  not not_94 (not_94_out, E);
  not not_95 (not_95_out, A);
  not not_96 (not_96_out, D);
  not not_97 (not_97_out, D);
  not not_98 (not_98_out, A);
  not not_99 (not_99_out, C);
  not not_100 (not_100_out, E);
  not not_101 (not_101_out, B);
  and and_1 (and_1_out, not_1_out, not_2_out, not_3_out);
  and and_2 (and_2_out, not_4_out, D);
  and and_3 (and_3_out, not_5_out, C, E);
  and and_4 (and_4_out, not_6_out, B, not_7_out);
  and and_5 (and_5_out, B, C, not_8_out);
  and and_6 (and_6_out, A, not_9_out, not_10_out);
  and and_7 (and_7_out, A, not_11_out, E);
  and and_8 (and_8_out, A, D, not_12_out);
  and and_9 (and_9_out, not_13_out, not_14_out);
  and and_10 (and_10_out, not_15_out, not_16_out, not_17_out);
  and and_11 (and_11_out, not_18_out, not_19_out, E);
  and and_12 (and_12_out, not_20_out, not_21_out, D);
  and and_13 (and_13_out, not_22_out, D, E);
  and and_14 (and_14_out, not_23_out, D, E);
  and and_15 (and_15_out, not_24_out, B, not_25_out);
  and and_16 (and_16_out, not_26_out, B, not_27_out);
  and and_17 (and_17_out, B, not_28_out, not_29_out);
  and and_18 (and_18_out, A, C);
  and and_19 (and_19_out, not_30_out, not_31_out);
  and and_20 (and_20_out, not_32_out, not_33_out);
  and and_21 (and_21_out, not_34_out, not_35_out, C);
  and and_22 (and_22_out, B, D);
  and and_23 (and_23_out, A, not_36_out);
  and and_24 (and_24_out, A, not_37_out);
  and and_25 (and_25_out, not_38_out, not_39_out, not_40_out);
  and and_26 (and_26_out, not_41_out, not_42_out, not_43_out);
  and and_27 (and_27_out, not_44_out, not_45_out, not_46_out, D);
  and and_28 (and_28_out, not_47_out, D, not_48_out);
  and and_29 (and_29_out, not_49_out, D, not_50_out);
  and and_30 (and_30_out, not_51_out, C, not_52_out, E);
  and and_31 (and_31_out, not_53_out, B, not_54_out, not_55_out);
  and and_32 (and_32_out, not_56_out, B, C, E);
  and and_33 (and_33_out, A, C, not_57_out);
  and and_34 (and_34_out, A, not_58_out, C, D);
  and and_35 (and_35_out, A, B, not_59_out, not_60_out, E);
  and and_36 (and_36_out, not_61_out, not_62_out, not_63_out);
  and and_37 (and_37_out, not_64_out, not_65_out, not_66_out);
  and and_38 (and_38_out, not_67_out, D, not_68_out);
  and and_39 (and_39_out, not_69_out, D, not_70_out);
  and and_40 (and_40_out, not_71_out, B, not_72_out, not_73_out);
  and and_41 (and_41_out, A, C, not_74_out);
  and and_42 (and_42_out, not_75_out, not_76_out, not_77_out);
  and and_43 (and_43_out, not_78_out, not_79_out, C, not_80_out);
  and and_44 (and_44_out, not_81_out, not_82_out, C, not_83_out);
  and and_45 (and_45_out, B, not_84_out, not_85_out);
  and and_46 (and_46_out, B, D, not_86_out);
  and and_47 (and_47_out, not_87_out, B, C, D);
  and and_48 (and_48_out, A, not_88_out, not_89_out, D);
  and and_49 (and_49_out, A, B, not_90_out);
  and and_50 (and_50_out, not_91_out, not_92_out, D);
  and and_51 (and_51_out, not_93_out, D, not_94_out);
  and and_52 (and_52_out, not_95_out, C, not_96_out);
  and and_53 (and_53_out, B, not_97_out);
  and and_54 (and_54_out, not_98_out, B, C);
  and and_55 (and_55_out, A, not_99_out, not_100_out);
  and and_56 (and_56_out, A, not_101_out, D);
  or or_1 (a_2, and_1_out, and_2_out, and_3_out, and_4_out, and_5_out, and_6_out, and_7_out, and_8_out);
  or or_2 (b_2, and_9_out, and_10_out, and_11_out, and_12_out, and_13_out, and_14_out, and_15_out, and_16_out, and_17_out, and_18_out);
  or or_3 (c_2, and_19_out, and_20_out, E, and_21_out, and_22_out, and_23_out, and_24_out);
  or or_4 (d_2, and_25_out, and_26_out, and_27_out, and_28_out, and_29_out, and_30_out, and_31_out, and_32_out, and_33_out, and_34_out, and_35_out);
  or or_5 (e_2, and_36_out, and_37_out, and_38_out, and_39_out, and_40_out, and_41_out);
  or or_6 (f, and_42_out, and_43_out, and_44_out, and_45_out, and_46_out, and_47_out, and_48_out, and_49_out);
  or or_7 (g, and_50_out, and_51_out, and_52_out, and_53_out, and_54_out, and_55_out, and_56_out);
endmodule

module _7_seg_mais_sig (
  input  A,
  input  B,
  input  C,
  input  D,
  input  E,
  output a_2,
  output b_2,
  output c_2,
  output d_2,
  output e_2,
  output f,
  output g
);

  wire and_1_out, and_2_out, and_3_out, and_4_out, and_5_out, and_6_out, and_7_out, and_8_out, and_9_out,
       and_10_out, and_11_out, and_12_out, and_13_out, and_14_out, and_15_out, and_16_out, and_17_out,
       and_18_out, and_19_out, not_1_out, not_2_out, not_3_out, not_4_out, not_5_out, not_6_out, not_7_out,
       not_8_out, not_9_out, not_10_out, not_11_out, not_12_out, not_13_out, not_14_out, not_15_out,
       not_16_out, not_17_out, not_18_out, not_19_out, not_20_out, not_21_out, not_22_out, not_23_out,
       not_24_out, not_25_out, not_26_out, not_27_out, not_28_out;

  not not_1 (not_1_out, A);
  not not_2 (not_2_out, B);
  not not_3 (not_3_out, A);
  not not_4 (not_4_out, C);
  not not_5 (not_5_out, D);
  not not_6 (not_6_out, B);
  not not_7 (not_7_out, B);
  not not_8 (not_8_out, C);
  not not_9 (not_9_out, A);
  not not_10 (not_10_out, B);
  not not_11 (not_11_out, A);
  not not_12 (not_12_out, C);
  not not_13 (not_13_out, D);
  not not_14 (not_14_out, B);
  not not_15 (not_15_out, A);
  not not_16 (not_16_out, B);
  not not_17 (not_17_out, A);
  not not_18 (not_18_out, C);
  not not_19 (not_19_out, D);
  not not_20 (not_20_out, B);
  not not_21 (not_21_out, C);
  not not_22 (not_22_out, D);
  not not_23 (not_23_out, A);
  not not_24 (not_24_out, B);
  not not_25 (not_25_out, A);
  not not_26 (not_26_out, C);
  not not_27 (not_27_out, D);
  and and_1 (and_1_out, A, C);
  and and_2 (and_2_out, A, B);
  and and_3 (and_3_out, not_1_out, not_2_out);
  and and_4 (and_4_out, not_3_out, not_4_out, not_5_out);
  and and_5 (and_5_out, not_6_out, C);
  and and_6 (and_6_out, A, B);
  not not_28 (not_28_out, A);
  and and_7 (and_7_out, not_7_out, not_8_out);
  and and_8 (and_8_out, B, C, D);
  and and_9 (and_9_out, not_9_out, not_10_out);
  and and_10 (and_10_out, not_11_out, not_12_out, not_13_out);
  and and_11 (and_11_out, not_14_out, C);
  and and_12 (and_12_out, A, B);
  and and_13 (and_13_out, not_15_out, not_16_out);
  and and_14 (and_14_out, not_17_out, not_18_out, not_19_out);
  and and_15 (and_15_out, not_20_out, C);
  and and_16 (and_16_out, A, B, not_21_out);
  and and_17 (and_17_out, A, B, not_22_out);
  and and_18 (and_18_out, not_23_out, not_24_out);
  and and_19 (and_19_out, not_25_out, not_26_out, not_27_out);
  or or_1 (g, and_1_out, and_2_out);
  or or_2 (a_2, and_3_out, and_4_out, and_5_out, and_6_out);
  or or_3 (c_2, not_28_out, and_7_out, and_8_out);
  or or_4 (d_2, and_9_out, and_10_out, and_11_out, and_12_out);
  or or_5 (e_2, and_13_out, and_14_out, and_15_out, and_16_out, and_17_out);
  or or_6 (f, and_18_out, and_19_out);

  assign b_2 = 1'b1;
endmodule
